// Logisim project circuito_pi.circ as structural Verilog: 1 circuit, main circuit main
module main (
  input  A,
  input  B,
  input  C,
  input  A_2,
  input  B_2,
  input  C_2,
  output out_7,
  output out_8
);

  wire a_nb_c_out, a_nb_nc_out, a_nb_out, and_1_out, and_2_out, and_3_out, and_4_out, and_5_out, and_6_out,
       and_7_out, and_8_out, and_9_out, and_10_out, and_11_out, not_1_out, not_2_out, not_3_out, not_4_out,
       not_5_out, not_6_out, not_7_out, not_8_out, not_9_out, or_1_out, or_2_out, or_3_out, or_4_out;

  not not_1 (not_1_out, A_2);
  not not_2 (not_2_out, C_2);
  not not_3 (not_3_out, A_2);
  not not_4 (not_4_out, B_2);
  not not_5 (not_5_out, C_2);
  not not_6 (not_6_out, B_2);
  not not_7 (not_7_out, A);
  not not_8 (not_8_out, C);
  not not_9 (not_9_out, B);
  and and_1 (and_1_out, not_1_out, B_2);
  and and_2 (and_2_out, not_3_out, B_2);
  and and_3 (and_3_out, A_2, not_4_out);
  and and_4 (and_4_out, A_2, not_6_out);
  and and_5 (and_5_out, not_7_out, B);
  and a_nb (a_nb_out, A, not_9_out);
  and and_6 (and_6_out, and_1_out, not_2_out);
  and and_7 (and_7_out, and_2_out, C_2);
  and and_8 (and_8_out, and_3_out, not_5_out);
  and and_9 (and_9_out, and_4_out, C_2);
  and and_10 (and_10_out, and_5_out, not_8_out);
  and and_11 (and_11_out, C, and_5_out);
  and a_nb_nc (a_nb_nc_out, a_nb_out, not_8_out);
  and a_nb_c (a_nb_c_out, a_nb_out, C);
  or or_1 (or_1_out, and_6_out, and_7_out);
  or or_2 (or_2_out, and_8_out, and_9_out);
  or or_3 (or_3_out, and_10_out, and_11_out);
  or or_4 (or_4_out, a_nb_nc_out, a_nb_c_out);
  or or_5 (out_8, or_1_out, or_2_out);
  or or_6 (out_7, or_3_out, or_4_out);

  // Notes on the sheet:
  //   Primeira Versão do Circuito
  //   (!a*b)
  //   (!a*b*!c)
  //   (!a*b*c)
  //   Circuito Corrigido (igual ao código)
  //   (!a*b*!c) + (!a*b*c)
  //   (a*!b*!c) + (a*!b*c)
  //   (!a*b*!c) + (!a*b*c) + (a*!b*!c) + (a*!b*c)
endmodule
